# Fritzing sketch electric_schema (saved by Fritzing 0.9.6b)

parts:
  M1 = Stepper Motor - Bipolar
  M2 = RioRand LM2596
  M3 = RioRand LM2596
  VCC1 = Battery block 9V
  Pololu_A1 = Pololu A4988 [package=SO16]
  part = SO-24x [chip_label=SO-24x package=SO(x)]  # not connected
  U2 = LuaNode32 / ESP32 [part_number=ESP32S-PIN30]
  M4 = Stepper Motor - Bipolar
  Pololu_A2 = Pololu A4988 [package=SO16]
  S1 = Pushbutton [package=THT]
  S2 = Pushbutton [package=THT]
  J1 = Basic Servo
  C1 = Electrolytic Capacitor [capacitance=0.1mF voltage=35V package="0405 [SMD, electrolytic]"]  # not connected

nets:
  N1: M1.A, Pololu_A1.2B
  N2: M1.C, Pololu_A1.1A
  N3: M1.B, Pololu_A1.2A
  N4: M1.D, Pololu_A1.1B
  N5: M2.Pin_1, VCC1.+
  N6: M2.Pin_3, Pololu_A1.VMOT
  N7: M3.Pin_3, Pololu_A1.VDD
  N8: M3.Pin_4, Pololu_A1.GND#8
  N9: Pololu_A1.RESET, Pololu_A1.SLEEP
  N10: Pololu_A1.STEP, U2.D32
  N11: Pololu_A1.DIR, U2.D33
  N12: U2.RX2, Pololu_A2.DIR
  N13: U2.TX2, Pololu_A2.STEP
  N14: U2.D18, J1.pulse
  N15: U2.D23, S1.leg1
  N16: M4.A, Pololu_A2.2B
  N17: M4.C, Pololu_A2.1A
  N18: M4.B, Pololu_A2.2A
  N19: M4.D, Pololu_A2.1B
  N20: Pololu_A2.RESET, Pololu_A2.SLEEP
  N21: S1.leg0, S2.leg0

notes:
  DC-DC 8V
  DC-DC 5V
  Be careful: this pinout in not exactly the same as ESP32-WROOM-32D

custom parts:
  LuaNode32 / ESP32: New Image for LuaNode32 DOIT ESP32 DEVKIT V1. Base parts from LuaNode32 / ESP32 ESP32 based LuaNode32 by G.Noorlander DOIT Esp32 DevKit v1 (30 pins long, 11 pins width) by Werner Rothschopf (modified by vanepp Dec 2018)
