# Fritzing sketch esp32-cam-flashing (saved by Fritzing 1.0.0d)

parts:
  Mod1 = ESP32 - CAM
  Part1 = FTDI Basic Programmer

nets:
  N1: Mod1.5V, Part1.POWER
  GND: Mod1.GND, Mod1.IO0, Part1.GND
  N2: Mod1.VOT, Part1.RXI
  N3: Mod1.VOR, Part1.TXO

custom parts:
  ESP32 - CAM: The ESP32-CAM has a very competitive small-size camera module that can operate independently as a minimum system with a footprint of only 27*40.5*4.5mm and a deep sleep current of up to 6mA.
